# Fritzing sketch LCDx3 I2C + DHT11 (saved by Fritzing 0.9.3b)
breadboards: 1

parts:
  Part1 = Arduino Uno (Rev3)
  LCD_-_I2C1 = LCD screen - I2C
  LCD_-_I2C2 = LCD screen - I2C
  DHT1 = Humidity and Temperature Sensor DHT11
  R1 = Resistor [tolerance=±5% resistance=220 package=THT]
  R2 = PHOTOCELL [package=photocell-kit]
  R3 = 1200 Ω Resistor [package="0805 [SMD]"]
  S1 = Pushbutton [package="[THT]"]

nets:
  N1: Part1.A0, R2.P$1, R3.Pin_1
  N2: Part1.A4/SDA, LCD_-_I2C1.SDA, LCD_-_I2C2.SDA
  N3: Part1.A5/SCL, LCD_-_I2C1.SCL, LCD_-_I2C2.SCL
  N4: Part1.D0/RX, S1.Pin_1, S1.Pin_2
  N5: Part1.D2, DHT1.Data-signal, R1.Pin_0
  VCC: Part1.5V, LCD_-_I2C1.VCC, LCD_-_I2C2.VCC, DHT1.Vcc, R1.Pin_1, R2.P$2
  GND: Part1.GND, LCD_-_I2C1.GND, LCD_-_I2C2.GND, DHT1.GND_2, R3.Pin_0, S1.Pin_3, S1.Pin_4

custom parts:
  LCD screen - I2C: A standard character display, usually with 2x16 characters. Comes in many colors.
  Humidity and Temperature Sensor DHT11: Digital relative humidity & temperature sensor DHT11
  1200 Ω Resistor: A generic resistor
